# Fritzing sketch Basic MIDI Controller (saved by Fritzing 0.9.2b)
breadboards: 1

parts:
  S1 = Pushbutton [package="[THT]"]
  S2 = Pushbutton [package="[THT]"]
  S3 = Pushbutton [package="[THT]"]
  S4 = Pushbutton [package="[THT]"]
  Part1 = Arduino Leonardo (Rev3b)
  R1 = Resistor [tolerance=±5% resistance=10k package=THT]
  R2 = Resistor [tolerance=±5% resistance=10k package=THT]
  R3 = Resistor [tolerance=±5% resistance=10k package=THT]
  R4 = Resistor [tolerance=±5% resistance=10k package=THT]

nets:
  N1: S1.Pin_1, S1.Pin_2, S2.Pin_1, S2.Pin_2, S3.Pin_1, S3.Pin_2, S4.Pin_1, S4.Pin_2, Part1.5V, Part1.D9_PWM/A9
  N2: S1.Pin_3, S1.Pin_4, Part1.D11_PWM, R1.Pin_0
  N3: S2.Pin_3, S2.Pin_4, Part1.D10_PWM/A10, R2.Pin_0
  N4: S3.Pin_3, S3.Pin_4, R3.Pin_0
  N5: S4.Pin_3, S4.Pin_4, Part1.D8/A8, R4.Pin_0
  N6: Part1.GND, R1.Pin_1, R2.Pin_1, R3.Pin_1, R4.Pin_1
